# Fritzing sketch fritzing project (saved by Fritzing 0.9.2b)
breadboards: 2

parts:
  Part1 = Arduino Uno (Rev3)
  U1 = MAX7219 [package=dil24]
  7_Segment1 = 7 Segment Display
  7_Segment2 = 7 Segment Display
  7_Segment3 = 7 Segment Display
  7_Segment4 = 7 Segment Display
  7_Segment5 = 7 Segment Display
  7_Segment6 = 7 Segment Display
  C1 = Capacitor Polarized [package=cpol-radial-10uf-25v]
  R1 = Resistor [tolerance=±5% resistance=10k package="0603 [SMD]"]
  C2 = Ceramic Capacitor [capacitance="100 nF" package="0805 [SMD, multilayer]"]
  S1 = Pushbutton [package="[THT]"]
  S2 = Pushbutton [package="[THT]"]
  S3 = Pushbutton [package="[THT]"]
  S4 = Pushbutton [package="[THT]"]
  S5 = Pushbutton [package="[THT]"]
  Part2 = LCD1602-I2C

nets:
  N1: Part1.A4/SDA, Part2.SDA
  N2: Part1.A5/SCL, Part2.SCL
  N3: Part1.D10_PWM/SS, U1.CLK
  N4: Part1.D11_PWM/MOSI, U1.LOAD
  N5: Part1.D12/MISO, U1.DIN
  N6: Part1.D2, S5.Pin_3, S5.Pin_4
  N7: Part1.D3_PWM, S4.Pin_3, S4.Pin_4
  N8: Part1.D4, S3.Pin_3, S3.Pin_4
  N9: Part1.D5_PWM, S2.Pin_3, S2.Pin_4
  N10: Part1.D6_PWM, S1.Pin_3, S1.Pin_4
  VCC: Part1.5V, U1.VCC, C1.+, R1.Pin_1, C2.0, Part2.VCC
  GND: Part1.GND, U1.GND, U1.GND2, C1.-, C2.1, S1.Pin_1, S1.Pin_2, S2.Pin_1, S2.Pin_2, S3.Pin_1, S3.Pin_2, S4.Pin_1, S4.Pin_2, S5.Pin_1, S5.Pin_2, Part2.GND
  N11: U1.DIG0, 7_Segment6.common_cathode
  N12: U1.DIG4, 7_Segment4.common_cathode
  N13: U1.DIG2, 7_Segment2.common_cathode
  N14: U1.DIG3, 7_Segment3.common_cathode
  N15: U1.DIG5, 7_Segment5.common_cathode
  N16: U1.DIG1, 7_Segment1.common_cathode
  N17: U1.SEGA, 7_Segment6.Segment_A
  N18: U1.SEGF, 7_Segment5.Segment_F
  N19: U1.SEGB, 7_Segment6.Segment_B
  N20: U1.SEGG, 7_Segment5.Segment_G
  N21: U1.ISET, R1.Pin_0
  N22: U1.SEGC, 7_Segment6.Segment_C
  N23: U1.SEGE, 7_Segment6.Segment_E
  N24: U1.SEGD, 7_Segment6.Segment_D

custom parts:
  LCD1602-I2C: A standard character display, usually with 2x16 characters. Comes in many colors with LCM1602 IIC attached.

// code stored in the sketch: main.ino
/*  Scoreboard designed for badminton
 * 
 *  Program designed for:
 *      -Arduino UNO
 *      -LCD i2c 1602 display
 *      -5 pushbuttons
 *      -6 - 7 segment common cathode displays
 *      -MAX 7219 chip
 *      
 *  fritzing project avaiable
 *  Shematics avaiable soon
 *    
 *  Features:
 *      -score reset without restarting arduino
 *      -changing sides by pressing a button
 *      -judge display
 *    
 *  Author: KRYSTIAN SLIWINSKI
 *  Contact: kskrystiansliwniski@gmail.com
 *  github: https://github.com/Infor-Tech
 */

//included libraries 
#include <LedControl.h>
#include "LiquidCrystal_I2C.h"
#include "wire.h"

//MAX7219 connection to Arduino
//LedControl(DIN, CLK, LOAD, number of MAX7219 chips)
LedControl lc = LedControl(12, 10, 11, 1);

//Set the LCD address to 0x27 for a 1602 display
LiquidCrystal_I2C lcd(0x27, 20, 4);

//scores variables
int ptk1 = 0; //Player 1 score
int ptk2 = 0; //Player 2 score
int s1 = 0; //Player 1 sets won
int s2 = 0; //Player 2 sets won

//variable defining on which side are players
int side = 0;

//variables to split whole number
int LeftDigit;
int RightDigit;

//startup variable
int startup = 0;

//Switches pin connection to Arduino
#define AddScore1 2   //player 1
#define AddScore2 3   //player 2 
#define SubScore 4
#define ChangeSides 5
#define ScoreReset 6

//displaying all data on LCD
void interface() {
    lcd.clear();
    lcd.print("Player 1: ");
    lcd.print(ptk1);
    lcd.setCursor(14,0);
    lcd.print("|");
    lcd.print(s1);
    lcd.setCursor(0, 1);
    lcd.print("Player 2: ");
    lcd.print(ptk2);
    lcd.setCursor(14,1);
    lcd.print("|");
    lcd.print(s2);
}

//Displaying score on 7 segment displays depends on side variable
//On deafult Player 1 is on left side
void ScorePrint() {
    if(side == 0){
  //Player 1 score
      RightDigit=ptk1%10;
      LeftDigit=ptk1%100/10;
      lc.setDigit(0,1,LeftDigit,false);
      lc.setDigit(0,2,RightDigit,false);
      lc.setDigit(0,0,s1,false);
      
  //Player 2 score
      RightDigit=ptk2%10;
      LeftDigit=ptk2%100/10;
      lc.setDigit(0,3,LeftDigit,false);
      lc.setDigit(0,4,RightDigit,false);
      lc.setDigit(0,5,s2, false);
    }else{
  //Player 1 score
      RightDigit=ptk1%10;
      LeftDigit=ptk1%100/10;
      lc.setDigit(0,3,LeftDigit,false);
      lc.setDigit(0,4,RightDigit,false);
      lc.setDigit(0,5,s1,false);
      
  //Player 2 score
      RightDigit=ptk2%10;
      LeftDigit=ptk2%100/10;
      lc.setDigit(0,1,LeftDigit,false);
      lc.setDigit(0,2,RightDigit,false);
      lc.setDigit(0,0,s2,false);
    }
}
    
void setup() {
//buttons pin mode
    pinMode(AddScore1, INPUT_PULLUP);
    pinMode(AddScore2, INPUT_PULLUP);
    pinMode(SubScore, INPUT_PULLUP);
    pinMode(ChangeSides, INPUT_PULLUP);
    pinMode(ScoreReset, INPUT_PULLUP);
    
//initialize the lcd
    lcd.init();
    lcd.backlight();
    
//initialize MAX7219
    lc.shutdown(0,false); //Turn on MAX7219
    lc.setIntensity(0,7); //Set brightness
    lc.clearDisplay(0); //Clear all displays connected to MAX7219
    
//startup screen
  //on lcd
    lcd.print("   github.com/");
    lcd.setCursor(3, 1);
    lcd.print("Infor-Tech");

  //on 7 segment display
  //displaying numbers 0-9
    for(startup = 0; startup <= 9; startup++){
      lc.setDigit(0,0,startup,false); //left set count
      lc.setDigit(0,1,startup,false); //left score
      lc.setDigit(0,2,startup,false); //left score
      lc.setDigit(0,3,startup,false); //right score
      lc.setDigit(0,4,startup,false); // right score
      lc.setDigit(0,5,startup,false); // right set count
      delay(400);
    }

  //after startup
    interface();
    ScorePrint();
    
}

void loop() {
//When side=0 on 7 segment displays player 1 is on a left
    if(!digitalRead(ChangeSides)) {
      if(side == 0){
        side = 1;
      }else{
        side = 0;
      }
      ScorePrint();
      delay(750);
    }

//When AddScore1 pressed there is added point for Player1 on lcd and 7 segment display
    if(!digitalRead(AddScore1)){
      ptk1++;
      interface();
      ScorePrint();
      delay(750);
    }

//When AddScore2 pressed there is added point for Player 2 on lcd and 7 segment display
    if(!digitalRead(AddScore2)){
      ptk2++;
      interface();
      ScorePrint();
      delay(750);
    }

//Reset scoreboard
    if(!digitalRead(ScoreReset)){
      ptk1 = 0;
      ptk2 = 0;
      s1 = 0;
      s2 = 0;
      side = 0;
      ScorePrint();
      interface();
      delay(750);
    }

//Subtract point from both players
    if(!digitalRead(SubScore)){
      ptk1 = ptk1 - 1;
      ptk2 = ptk2 - 1;
      ScorePrint();
      interface();
      delay(750);
    }

  //When Player 1 won set
    if(ptk1 >= 21 && ptk1 - ptk2 >= 2){
      s1 = s1 + 1;
      ptk1 = 0;
      ptk2 = 0;
      if(side == 0){
        side = 1;
      }else{
        side = 0;
      }
      delay(10000);
      interface();
      ScorePrint();
    }

  //When Player 2 won set
    if(ptk2 >= 21 && ptk2 - ptk1 >= 2){
      s2 = s2 + 1;
      ptk1 = 0;
      ptk2 = 0;
      if(side == 0){
        side = 1;
      }else{
        side = 0;
      }
      delay(10000);
      interface();
    }
}
